# Fritzing sketch Schema (saved by Fritzing 0.9.3b)

parts:
  R1 = Resistor [tolerance=±5% resistance=220 package=THT]
  LED1 = LED - 5mm [color="Yellow (595nm)" package="5 mm [THT]"]
  Part1 = Arduino Nano (Rev3.0)
  R2 = Resistor [tolerance=±5% resistance=220 package=THT]
  LED2 = LED - 5mm [color="Yellow (595nm)" package="5 mm [THT]"]
  R3 = Resistor [tolerance=±5% resistance=220 package=THT]
  LED3 = LED - 5mm [color="Yellow (595nm)" package="5 mm [THT]"]
  R4 = Resistor [tolerance=±5% resistance=220 package=THT]
  LED4 = LED - 5mm [color="Yellow (595nm)" package="5 mm [THT]"]
  R5 = Resistor [tolerance=±5% resistance=220 package=THT]
  LED5 = LED - 5mm [color="White (4500K)" package="5 mm [THT]"]

nets:
  N1: R1.Pin_0, R2.Pin_0, R3.Pin_0, R4.Pin_0, R5.Pin_0
  N2: R1.Pin_1, LED1.cathode
  N3: LED1.anode, Part1.D2
  N4: Part1.D3, LED2.anode
  N5: Part1.D4, LED3.anode
  N6: Part1.D5, LED4.anode
  N7: Part1.D10, LED5.anode
  N8: R2.Pin_1, LED2.cathode
  N9: R3.Pin_1, LED3.cathode
  N10: R4.Pin_1, LED4.cathode
  N11: R5.Pin_1, LED5.cathode
